# Fritzing sketch Sketch (saved by Fritzing 0.9.6b)
breadboards: 1

parts:
  RHT2 = Humidity and Temperature Sensor RHT03 [part_number=DHT22]
  R1 = Resistor [tolerance=±5% resistance=220 package="2512 [SMD]"]
  Raspberry_Pi_1 = Raspberry Pi 3 [part_number=RPI-3-V1.2]
  SH1106 = Grove OLED 128x96

nets:
  VCC: RHT2.Vcc, R1.Pin_0, Raspberry_Pi_1.5V, SH1106.VCC
  N1: RHT2.Data-signal, R1.Pin_1, Raspberry_Pi_1.GPIO14
  GND: RHT2.GND_2, Raspberry_Pi_1.GND, SH1106.GND
  N2: Raspberry_Pi_1.GPIO20, SH1106.SCL
  N3: Raspberry_Pi_1.GPIO16, SH1106.SDA
